# Fritzing sketch PCB_3.0 (saved by Fritzing 0.9.3b)
circuit board: 4.5cm x 9.5cm
breadboards: 1

parts:
  Arduino_NANO_Rev_3 = Arduino Nano (Rev3.0)
  470 = Resistor [tolerance=±5% resistance=470 package=THT]
  10k = Resistor [tolerance=±5% resistance=10k package=THT]
  1k1 = Resistor [tolerance=±5% resistance=1k package=THT]
  BC337 = TRANSISTOR_NPN [package=to-92-ammo]
  LED2 = LED - 3mm [color="Red (633nm)" package="3 mm [THT]"]
  D2 = Rectifier Diode [part_number=1N4148 package="300 mil [THT]"]
  RELAY = Relay T73
  7805 = Voltage Regulator - 5V [part_number=" 7805" package="TO220 [THT]"]
  C3 = Electrolytic Capacitor [capacitance=0.1µF package="100 mil [THT, electrolytic]"]
  1K = Resistor [tolerance=±10% resistance=1k package=THT]
  10k_2 = Resistor [tolerance=±5% resistance=10k package=THT]
  BC337_2 = TRANSISTOR_NPN [package=to-92-ammo]
  1N4007 = Rectifier Diode [part_number=1N4001 package="300 mil [THT]"]
  POWER = LED - 3mm [color="Red (633nm)" package="3 mm [THT]"]
  150 = Resistor [tolerance=±5% resistance=150 package=THT]
  100uF = Electrolytic Capacitor [capacitance=100nF voltage=50V package="100 mil [THT, electrolytic]"]
  100uF_2 = Tantalum Capacitor [capacitance=100nF voltage=50V package="100 mil [THT, tantalum]"]
  100nF = Tantalum Capacitor [capacitance=100nF voltage=50V package="100 mil [THT, tantalum]"]
  1N4007_2 = Rectifier Diode [part_number=1N4001 package="300 mil [THT]"]
  100uf = Electrolytic Capacitor [capacitance=1µF voltage=50V package="100 mil [THT, electrolytic]"]
  1N4007_3 = Rectifier Diode [part_number=1N4001 package="300 mil [THT]"]

nets:
  N1: Arduino_NANO_Rev_3.GND, 10k.Pin_1, BC337.E, BC337_2.C
  N2: Arduino_NANO_Rev_3.D2, 1k1.Pin_0
  N3: Arduino_NANO_Rev_3.D4, 10k_2.Pin_1
  N4: Arduino_NANO_Rev_3.D5, 1K.Pin_0
  N5: Arduino_NANO_Rev_3.5V, 1N4007_3.cathode
  N6: 470.Pin_0, D2.cathode, RELAY.C2, 7805.output_voltage, C3.+, 10k_2.Pin_0, 150.Pin_0, 100nF.-, 1N4007_3.anode
  N7: 470.Pin_1, LED2.anode
  N8: 10k.Pin_0, 1k1.Pin_1, BC337.B
  N9: BC337.C, LED2.cathode, D2.anode, RELAY.C1
  N10: 7805.input_voltage, 100uF.+, 100uF_2.-, 1N4007_2.cathode
  N11: 7805.GND, C3.-, 100uF.-, 100uF_2.+, 100nF.+
  N12: 1K.Pin_1, BC337_2.B, 100uf.+
  N13: BC337_2.E, 1N4007.anode
  N14: 1N4007.cathode, 1N4007_2.anode
  N15: POWER.anode, 150.Pin_1

notes:
  12v
  gnd comun
  1
  4
  DHT22
  1 2
  FAN
  +
  -
  resistencia
  termica
  A   B
  E  F   G
  2
  +5v comun
  SDA
  SCL
  Filament Dryer
  PCB 3
  Damian Martinez Sanchez
  termal led
  P2
  P1

custom parts:
  Relay T73: An T73 Mini PCB Relay
