# Fritzing sketch conector_12v (saved by Fritzing 0.9.3b)
circuit board: 1.5cm x 4cm
breadboards: 1

parts:
  J1 = Power Jack [package=power_jack_pth_lock]

nets:
  N1: J1.GND, J1.GNDBREAK

notes:
  -
  +
  Filament
  Dryer
  Damian Martinez Sanchez
