# Fritzing sketch panel_control (saved by Fritzing 0.9.3b)
circuit board: 3.7cm x 6.1cm
breadboards: 1

parts:
  hot = LED - 3mm [color="Red (633nm)" package="3 mm [THT]"]
  cold = LED - 3mm [color="Red (633nm)" package="3 mm [THT]"]
  LED3 = LED - 3mm [color="Red (633nm)" package="3 mm [THT]"]  # not connected
  10o = Resistor [tolerance=±5% resistance=10 package=THT]
  S5 = Pushbutton [package="[THT]"]
  S6 = Pushbutton [package="[THT]"]
  S8 = Pushbutton [package="[THT]"]
  10o_2 = Resistor [tolerance=±5% resistance=10 package=THT]
  10o_3 = Resistor [tolerance=±5% resistance=10 package=THT]
  220 = Resistor [tolerance=±5% resistance=220 package=THT]
  220_2 = Resistor [tolerance=±5% resistance=220 package=THT]

nets:
  N1: hot.anode, 220.Pin_1
  N2: cold.anode, 220_2.Pin_1
  N3: 10o.Pin_1, S6.Pin_1, S6.Pin_2
  N4: S5.Pin_2, 10o_2.Pin_1
  N5: S5.Pin_3, S5.Pin_4, S6.Pin_3, S6.Pin_4, S8.Pin_3
  N6: S8.Pin_2, 10o_3.Pin_1

notes:
  gnd
  vcc
  scl
  sda
  Damian Martinez Sanchez
  Secador de Filamento 3D
  P2
  P1
  A
  B
  E
  G
  F
  termal led
